# Fritzing sketch smart-plant-watering-system (saved by Fritzing 0.9.6b)

parts:
  L298N1 = L298N DC motor driver
  U1 = ESP32S-HiLetgo [part_number=ESP32S-HiLetgo]
  M1 = DC Motor
  R1 = Resistor [tolerance=±5% resistance=220 package="0603 [SMD]"]
  R2 = Resistor [tolerance=±5% resistance=220 package="0603 [SMD]"]
  LED1 = smd LED [color="Red (633nm)" package="0603 [SMD]"]
  LED2 = smd LED [color="Yellow (595nm)" package="0603 [SMD]"]
  HC-SR04_Sensor_1 = HC-SR04 Ultrasonic Distance Sensor
  S1 = Pushbutton [package="[THT]"]
  Capacitive_Soil_Moisture_Sensor1 = DFRobot Capacitive Soil Moisture Sensor V1.0 [part_number=SEN0193]
  Capacitive_Soil_Moisture_Sensor2 = DFRobot Capacitive Soil Moisture Sensor V1.0 [part_number=SEN0193]
  R3 = Photocell (LDR) [package=THT]
  R4 = Resistor [tolerance=±5% resistance=220 package="0603 [SMD]"]
  R5 = Resistor [tolerance=±5% resistance=220 package="0603 [SMD]"]
  R6 = Resistor [tolerance=±5% resistance=220 package="0603 [SMD]"]
  M2 = DC Motor

nets:
  N1: L298N1.OUT1, M2.pin_2
  N2: L298N1.OUT2, M2.pin_1
  N3: L298N1.OUT3, M1.pin_2
  N4: L298N1.OUT4, M1.pin_1
  GND: L298N1.GND, U1.GND, R1.Pin_1, R2.Pin_1, HC-SR04_Sensor_1.GND, Capacitive_Soil_Moisture_Sensor1.GND, Capacitive_Soil_Moisture_Sensor2.GND, R4.Pin_1, R6.Pin_1
  VIN: L298N1.5V#7, U1.GPIO11, U1.VIN, HC-SR04_Sensor_1.VCC
  N5: L298N1.5V#9, L298N1.ENA
  N6: L298N1.5V#10, L298N1.ENB
  N7: L298N1.IN2, U1.GPIO16
  N8: L298N1.IN3, U1.GPIO4
  VCC: U1.3.3, S1.Pin_1, S1.Pin_2, Capacitive_Soil_Moisture_Sensor1.VCC, Capacitive_Soil_Moisture_Sensor2.VCC, R3.pin_1
  N9: U1.EN, U1.GPIO36, R3.pin_0, R5.Pin_0
  N10: U1.GPIO39, U1.GPIO34, Capacitive_Soil_Moisture_Sensor2.A
  N11: U1.GPIO35, Capacitive_Soil_Moisture_Sensor1.A
  N12: U1.GPIO27, U1.GPIO14, HC-SR04_Sensor_1.TRIG
  N13: U1.GPIO12, HC-SR04_Sensor_1.ECHO
  N14: U1.GPIO13, S1.Pin_3, S1.Pin_4, R4.Pin_0
  N15: U1.GPIO17, LED2.anode
  N16: U1.GPIO5, U1.GPIO18, LED1.anode
  N17: R1.Pin_0, LED2.cathode
  N18: R2.Pin_0, LED1.cathode
  N19: R5.Pin_1, R6.Pin_0

notes:
  9-12 V DC Power
  9-12 V DC Pump 2
  9-12 V DC Pump 1
  Moisture Sensor 1
  Light Sensor
  Ultrasonice Sensor
  Moisture Sensor 2
  Button
  LEDs
  ESP 32 Board
  L298N

custom parts:
  L298N DC motor driver: 2x DC motor driver with 78M05 positive voltage regulator (7..35 V) L298N: max 46 V, 2 A Set 5 V Enable jumper to enable 5 V regultor (needed for the L298N) and +5 V output at screw terminal or supply external +5 V at screw terminal Set ENA and/or ENB to +5 V to enable motor permanently or supply ENA and/or ENB with PWM signal IN1 and IN2 set rotation directory for motor A (OUT1/OUT2) IN2 and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
  ESP32S-HiLetgo: HiLetgo ESP-WROOM-32 ESP32 ESP-32S Development Board 2.4GHz Dual-Mode WiFi + Bluetooth Dual Cores Microcontroller The ESP32 integrated with Antenna switches, RF Balun, power amplifiers, low-noise amplifiers, filters, and management modules, and the entire solution occupies the least area of PCB. 2.4 GHz Wi-Fi plus Bluetooth dual-mode chip, with TSMC Ultra-low power consumption 40nm technology,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
  DFRobot Capacitive Soil Moisture Sensor V1.0: DFRobot Capacitive Soil Moisture Sensor V1.0 This product measures soil moisture levels by capacitive sensing, rather than resistive sensing like other types of moisture sensor. It is made of a corrosion resistant material giving it a long service life. Insert it into soil and impress your friends with the real-time soil moisture data! The product includes an on-board voltage regulator which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
